// Logisim project miniCurso.circ as structural Verilog: 14 circuits, main circuit main
module main (
  input  in_1,
  input  in_2,
  input  in_3,
  input  in_4,
  input  in_5,
  input  in_6,
  input  in_7,
  input  in_8,
  input  [1:0] in_9,
  input  in_10,
  input  in_11,
  input  in_12,
  input  in_13,
  input  [1:0] in_14,
  input  [1:0] in_15,
  input  [1:0] in_16,
  input  [1:0] in_17,
  input  [1:0] in_18,
  input  [1:0] in_19,
  input  [7:0] in_20,
  input  [7:0] in_21,
  input  [1:0] in_22,
  output out_23,
  output out_24,
  output out_25,
  output out_26,
  output out_27,
  output [1:0] out_28,
  output out_29,
  output out_30,
  output out_31,
  output out_32,
  output [7:0] out_33
);

  wire [7:0] adder_1_out, and_1_out, or_1_out, subtractor_1_out;

  Multiplexer #(.select(2), .enable("false")) multiplexer_1 (
    .in0(in_10), .in1(in_11), .in2(in_12), .in3(in_13), .out(out_27), .sel(in_9));
  Decoder #(.select(2), .enable("false")) decoder_1 (
    .out0(out_29), .out1(out_30), .out2(out_31), .out3(out_32), .sel(in_19));
  nand nand_1 (out_23, in_1, in_2);
  nor nor_1 (out_24, in_3, in_4);
  Multiplexer #(.select(2), .width(2), .enable("false")) multiplexer_2 (
    .in0(in_14), .in1(in_15), .in2(in_16), .in3(in_17), .out(out_28), .sel(in_18));
  Adder adder_1 (.a(in_21), .b(in_20), .out(adder_1_out));  // open: cin, cout
  Subtractor subtractor_1 (.a(in_21), .b(in_20), .out(subtractor_1_out));  // open: bin, bout
  assign and_1_out = in_21 & in_20;  // AND_Gate and_1, 8 bits wide
  assign or_1_out = in_21 | in_20;  // OR_Gate or_1, 8 bits wide
  Multiplexer #(.select(2), .width(8)) multiplexer_3 (
    .in0(adder_1_out), .in1(subtractor_1_out), .in2(and_1_out), .in3(or_1_out), .out(out_33), .sel(in_22));  // open: en
  xor xor_1 (out_25, in_5, in_6);
  xnor xnor_1 (out_26, in_7, in_8);

  // Notes on the sheet:
  //   Mini Curso 
endmodule

module HalfAdder (
  input  A,
  input  B,
  output carry_in,
  output SomaAB
);

  and and_1 (carry_in, A, B);
  xor xor_1 (SomaAB, A, B);
endmodule

module FullAdder (
  input  A,
  input  B,
  input  carry_in,
  output carry_out_final,
  output S
);

  wire and_1_out, and_2_out, xor_1_out;

  and and_1 (and_1_out, A, B);
  xor xor_1 (xor_1_out, A, B);
  xor xor_2 (S, xor_1_out, carry_in);
  and and_2 (and_2_out, xor_1_out, carry_in);
  or or_1 (carry_out_final, and_1_out, and_2_out);

  // Notes on the sheet:
  //   carry out1
  //   S1
  //                     carry out2
endmodule

module FullAdderWithTwoHalfAdder (
  input  A,
  input  B,
  input  carry_in,
  output carry_out,
  output Soma_Final
);

  wire halfadder_1_carry_in, halfadder_1_somaab, halfadder_2_carry_in;

  HalfAdder halfadder_1 (.A(A), .B(B), .carry_in(halfadder_1_carry_in), .SomaAB(halfadder_1_somaab));
  HalfAdder halfadder_2 (.A(halfadder_1_somaab), .B(carry_in), .carry_in(halfadder_2_carry_in), .SomaAB(Soma_Final));
  or or_1 (carry_out, halfadder_1_carry_in, halfadder_2_carry_in);
endmodule

module RippleCarryAdder (
  input  [7:0] A,
  input  in_2,
  input  [7:0] B,
  input  in_4,
  input  in_5,
  input  in_6,
  input  in_7,
  input  in_8,
  input  in_9,
  input  in_10,
  input  in_11,
  input  in_12,
  input  in_13,
  input  in_14,
  input  in_15,
  input  in_16,
  input  in_17,
  input  in_18,
  input  in_19,
  input  in_20,
  output out_21,
  output [7:0] Resultado_Soma,
  output out_23,
  output out_24,
  output out_25,
  output out_26,
  output out_27,
  output out_28,
  output out_29,
  output out_30,
  output out_31
);

  wire fulladder_2_carry_out_final, fulladder_3_carry_out_final, fulladder_4_carry_out_final,
       fulladder_5_carry_out_final, fulladder_6_carry_out_final, fulladder_7_carry_out_final,
       fulladder_8_carry_out_final, fulladder_9_carry_out_final, fulladder_10_carry_out_final,
       fulladder_11_carry_out_final, fulladder_12_carry_out_final, fulladder_13_carry_out_final,
       fulladder_14_carry_out_final, fulladder_15_carry_out_final;

  FullAdder fulladder_1 (
    .A(A[7]), .B(B[7]), .carry_in(fulladder_3_carry_out_final), .carry_out_final(out_21),
    .S(Resultado_Soma[7]));
  FullAdder fulladder_2 (
    .A(in_5), .B(in_6), .carry_in(in_4), .carry_out_final(fulladder_2_carry_out_final), .S(out_23));
  FullAdder fulladder_3 (
    .A(A[6]), .B(B[6]), .carry_in(fulladder_5_carry_out_final),
    .carry_out_final(fulladder_3_carry_out_final), .S(Resultado_Soma[6]));
  FullAdder fulladder_4 (
    .A(in_7), .B(in_8), .carry_in(fulladder_2_carry_out_final),
    .carry_out_final(fulladder_4_carry_out_final), .S(out_24));
  FullAdder fulladder_5 (
    .A(A[5]), .B(B[5]), .carry_in(fulladder_6_carry_out_final),
    .carry_out_final(fulladder_5_carry_out_final), .S(Resultado_Soma[5]));
  FullAdder fulladder_6 (
    .A(A[4]), .B(B[4]), .carry_in(fulladder_8_carry_out_final),
    .carry_out_final(fulladder_6_carry_out_final), .S(Resultado_Soma[4]));
  FullAdder fulladder_7 (
    .A(in_9), .B(in_10), .carry_in(fulladder_4_carry_out_final),
    .carry_out_final(fulladder_7_carry_out_final), .S(out_25));
  FullAdder fulladder_8 (
    .A(A[3]), .B(B[3]), .carry_in(fulladder_10_carry_out_final),
    .carry_out_final(fulladder_8_carry_out_final), .S(Resultado_Soma[3]));
  FullAdder fulladder_9 (
    .A(in_11), .B(in_12), .carry_in(fulladder_7_carry_out_final),
    .carry_out_final(fulladder_9_carry_out_final), .S(out_26));
  FullAdder fulladder_10 (
    .A(A[2]), .B(B[2]), .carry_in(fulladder_12_carry_out_final),
    .carry_out_final(fulladder_10_carry_out_final), .S(Resultado_Soma[2]));
  FullAdder fulladder_11 (
    .A(in_13), .B(in_14), .carry_in(fulladder_9_carry_out_final),
    .carry_out_final(fulladder_11_carry_out_final), .S(out_27));
  FullAdder fulladder_12 (
    .A(A[1]), .B(B[1]), .carry_in(fulladder_14_carry_out_final),
    .carry_out_final(fulladder_12_carry_out_final), .S(Resultado_Soma[1]));
  FullAdder fulladder_13 (
    .A(in_15), .B(in_16), .carry_in(fulladder_11_carry_out_final),
    .carry_out_final(fulladder_13_carry_out_final), .S(out_28));
  FullAdder fulladder_14 (
    .A(A[0]), .B(B[0]), .carry_in(in_2), .carry_out_final(fulladder_14_carry_out_final), .S(Resultado_Soma[0]));
  FullAdder fulladder_15 (
    .A(in_17), .B(in_18), .carry_in(fulladder_13_carry_out_final),
    .carry_out_final(fulladder_15_carry_out_final), .S(out_29));
  FullAdder fulladder_16 (
    .A(in_19), .B(in_20), .carry_in(fulladder_15_carry_out_final), .carry_out_final(out_31), .S(out_30));
endmodule

module FlipFlopRSNand (
  input  S,
  input  R,
  output Q,
  output nQ
);

  nand nand_1 (Q, ~S, nQ);  // NAND_Gate
  nand nand_2 (nQ, Q, ~R);  // NAND_Gate
endmodule

module FlipFlopRSNandWithClock (
  input  S,
  input  R,
  output out_3,
  output out_4
);

  wire Clock_out, nand_1_out, nand_2_out;

  Clock Clock (.out(Clock_out));
  nand nand_1 (nand_1_out, S, Clock_out);
  nand nand_2 (nand_2_out, Clock_out, R);
  nand nand_3 (out_3, nand_1_out, out_4);
  nand nand_4 (out_4, out_3, nand_2_out);
endmodule

module FlipFlopSRNor (
  input  A,
  input  B,
  output Q,
  output nQ
);

  nor nor_1 (Q, A, nQ);
  nor nor_2 (nQ, Q, B);
endmodule

module FlipFlopJK (
  input  J,
  input  K,
  output Q,
  output nQ
);

  wire clock_1_out;

  Clock clock_1 (.out(clock_1_out));
  J_K_Flip_Flop j_k_ff_1 (.J(J), .clk(clock_1_out), .K(K), .Q(Q), .Qn(nQ));  // open: preset, en, reset

  // Notes on the sheet:
  //   Infelizmente por causa das limitacões do logisim não foi possível implementar igual aos outros circutos
endmodule

module FlipFlopT (
  input  T,
  output Q,
  output nQ
);

  FlipFlopJK flipflopjk_1 (.J(T), .K(T), .Q(Q), .nQ(nQ));
endmodule

module FlipFlopD (
  input  D,
  output Q,
  output out_3
);

  wire not_1_out;

  not not_1 (not_1_out, D);
  FlipFlopJK flipflopjk_1 (.J(D), .K(not_1_out), .Q(Q), .nQ(out_3));
endmodule

module Register (
  input  [7:0] in_1,
  input  in_2,
  input  in_3,
  output [7:0] out_4
);

  wire clock_1_out;

  Register_part register_1 (.D(in_1), .en(in_2), .Q(out_4), .clk(clock_1_out), .clr(in_3));
  Clock clock_1 (.out(clock_1_out));
endmodule

module RegisterSISO (
  input  in_1,
  input  Preset,
  input  Enable,
  input  Clear,
  output out_5
);

  wire clock_1_out, d_ff_1_q, d_ff_2_q, d_ff_3_q;

  Clock clock_1 (.out(clock_1_out));
  D_Flip_Flop d_ff_1 (
    .clk(clock_1_out), .D(in_1), .Q(d_ff_1_q), .preset(Preset), .en(Enable), .reset(Clear));  // open: Qn
  D_Flip_Flop d_ff_2 (
    .clk(clock_1_out), .D(d_ff_1_q), .Q(d_ff_2_q), .preset(Preset), .en(Enable), .reset(Clear));  // open: Qn
  D_Flip_Flop d_ff_3 (
    .clk(clock_1_out), .D(d_ff_2_q), .Q(d_ff_3_q), .preset(Preset), .en(Enable), .reset(Clear));  // open: Qn
  D_Flip_Flop d_ff_4 (
    .clk(clock_1_out), .D(d_ff_3_q), .Q(out_5), .preset(Preset), .en(Enable), .reset(Clear));  // open: Qn
endmodule

module RegisterPIPO (
  input  [3:0] In,
  output [3:0] Out
);

  wire clock_1_out;

  Clock clock_1 (.out(clock_1_out));
  D_Flip_Flop d_ff_1 (.clk(clock_1_out), .D(In[3]), .Q(Out[3]));  // open: Qn, preset, en, reset
  D_Flip_Flop d_ff_2 (.clk(clock_1_out), .D(In[2]), .Q(Out[2]));  // open: Qn, preset, en, reset
  D_Flip_Flop d_ff_3 (.clk(clock_1_out), .D(In[1]), .Q(Out[1]));  // open: Qn, preset, en, reset
  D_Flip_Flop d_ff_4 (.clk(clock_1_out), .D(In[0]), .Q(Out[0]));  // open: Qn, preset, en, reset
endmodule
